# Fritzing sketch hall sensor (saved by Fritzing 0.9.6b)
breadboards: 1

parts:
  Part1 = Arduino Nano (Rev3.0)
  S1 = Hall Sensor [part_number=WSH130 package=TO92]

nets:
  GND: Part1.GND, S1.GND
  5V: Part1.5V, S1.VCC
  N1: Part1.A0, S1.OUT

custom parts:
  Hall Sensor: A Hall Sensor
